// Logisim project QuintenBallardGPP4bit.circ as structural Verilog: 16 circuits, main circuit MPP
module HalfAdder (
  input  a,
  input  b,
  output sum,
  output cout
);

  xor xor_1 (sum, a, b);
  and and_1 (cout, a, b);
endmodule

module FullAdder (
  input  cin,
  input  a,
  input  b,
  output sum,
  output cout
);

  wire halfadder_1_cout, halfadder_2_cout, halfadder_2_sum;

  HalfAdder halfadder_1 (.a(cin), .b(halfadder_2_sum), .sum(sum), .cout(halfadder_1_cout));
  or or_1 (cout, halfadder_1_cout, halfadder_2_cout);
  HalfAdder halfadder_2 (.a(a), .b(b), .sum(halfadder_2_sum), .cout(halfadder_2_cout));
endmodule

module FullAdder4bit (
  input  cin,
  input  [3:0] A,
  input  [3:0] B,
  output [3:0] sum,
  output cout
);

  wire fulladder_1_cout, fulladder_2_cout, fulladder_3_cout;

  FullAdder fulladder_1 (.cin(cin), .a(A[0]), .b(B[0]), .sum(sum[0]), .cout(fulladder_1_cout));
  FullAdder fulladder_2 (.cin(fulladder_1_cout), .a(A[1]), .b(B[1]), .sum(sum[1]), .cout(fulladder_2_cout));
  FullAdder fulladder_3 (.cin(fulladder_2_cout), .a(A[2]), .b(B[2]), .sum(sum[2]), .cout(fulladder_3_cout));
  FullAdder fulladder_4 (.cin(fulladder_3_cout), .a(A[3]), .b(B[3]), .sum(sum[3]), .cout(cout));
endmodule

module ALU (
  input  [3:0] A,
  input  [3:0] B,
  input  [2:0] opcode,
  output [3:0] F,
  output Z,
  output N,
  output V
);

  wire and_2_out, and_3_out, multiplexer_1_out, not_2_out, not_3_out, not_4_out;
  wire [3:0] and_1_out, multiplexer_2_out, multiplexer_3_out, not_1_out, or_1_out, xor_1_out;

  assign xor_1_out = A ^ B;  // XOR_Gate xor_1, 4 bits wide
  assign and_1_out = A & B;  // AND_Gate and_1, 4 bits wide
  assign or_1_out = A | B;  // OR_Gate or_1, 4 bits wide
  assign not_1_out = ~B;  // NOT_Gate not_1, 4 bits wide
  Multiplexer #(.select(3)) multiplexer_1 (
    .in0(1'b0), .in1(1'b0), .in2(1'b0), .in3(1'b0), .in4(1'b0), .in5(1'b1), .in6(1'b1), .in7(1'b0),
    .out(multiplexer_1_out), .sel(opcode));
  Multiplexer #(.select(3), .width(4)) multiplexer_2 (
    .in0(4'b0000), .in1(4'b0000), .in2(4'b0000), .in3(4'b0000), .in4(A), .in5(A), .in6(4'b0000),
    .in7(4'b1111), .out(multiplexer_2_out), .sel(opcode));
  Multiplexer #(.select(3), .width(4)) multiplexer_3 (
    .in0(B), .in1(xor_1_out), .in2(and_1_out), .in3(or_1_out), .in4(B), .in5(not_1_out), .in6(B), .in7(B),
    .out(multiplexer_3_out), .sel(opcode));
  FullAdder4bit fulladder4bit_1 (
    .cin(multiplexer_1_out), .A(multiplexer_2_out), .B(multiplexer_3_out), .sum(F));  // open: cout
  not not_2 (not_2_out, multiplexer_2_out[3]);
  not not_3 (not_3_out, multiplexer_3_out[3]);
  and and_2 (and_2_out, not_2_out, not_3_out, F[3]);
  and and_3 (and_3_out, multiplexer_2_out[3], multiplexer_3_out[3], not_4_out);
  not not_4 (not_4_out, F[3]);
  nor nor_1 (Z, F[0], F[1], F[2], F[3]);
  or or_2 (V, and_2_out, and_3_out);

  assign N = F[3];
endmodule

module MPP (
  input  [3:0] data_in,
  input  reset,
  output [3:0] output_a,
  output [3:0] output_b
);

  wire alu_1_n, alu_1_v, alu_1_z, clock_1_out, controller_1_jump_enable, controller_1_use_input,
       controller_1_w_enable, d_ff_1_q, d_ff_2_q, d_ff_3_q, multiplexer_1_out, multiplexer_2_out,
       multiplexer_3_out;
  wire [1:0] controller_1_r_addr_a, controller_1_r_addr_b, controller_1_w_addr;
  wire [2:0] controller_1_opcode;
  wire [3:0] alu_1_f, controller_1_jump_addr, multiplexer_4_out, programcounter_1_i_addr;
  wire [8:0] rom_1_data;

  ROM #(.addrWidth(4), .dataWidth(9)) rom_1 (.addr(programcounter_1_i_addr), .data(rom_1_data));
  D_Flip_Flop d_ff_1 (.D(multiplexer_1_out), .clk(clock_1_out), .Q(d_ff_1_q), .reset(reset));  // open: Qn, preset
  Multiplexer multiplexer_1 (.in1(alu_1_v), .out(multiplexer_1_out), .sel(controller_1_w_enable));  // open: in0
  Clock clock_1 (.out(clock_1_out));
  D_Flip_Flop d_ff_2 (.D(multiplexer_2_out), .clk(clock_1_out), .Q(d_ff_2_q), .reset(reset));  // open: Qn, preset
  Multiplexer multiplexer_2 (.in1(alu_1_z), .out(multiplexer_2_out), .sel(controller_1_w_enable));  // open: in0
  ProgramCounter programcounter_1 (
    .jump_addr(controller_1_jump_addr), .jump_enable(controller_1_jump_enable), .clock(clock_1_out),
    .reset(reset), .i_addr(programcounter_1_i_addr));
  D_Flip_Flop d_ff_3 (.D(multiplexer_3_out), .clk(clock_1_out), .Q(d_ff_3_q), .reset(reset));  // open: Qn, preset
  Multiplexer multiplexer_3 (.in0(d_ff_3_q), .in1(alu_1_n), .out(multiplexer_3_out), .sel(controller_1_w_enable));
  Multiplexer #(.width(4)) multiplexer_4 (
    .in0(output_b), .in1(data_in), .out(multiplexer_4_out), .sel(controller_1_use_input));
  controller controller_1 (
    .instruction(rom_1_data), .V(d_ff_1_q), .Z(d_ff_2_q), .N(d_ff_3_q), .r_addr_a(controller_1_r_addr_a),
    .r_addr_b(controller_1_r_addr_b), .w_addr(controller_1_w_addr), .opcode(controller_1_opcode),
    .w_enable(controller_1_w_enable), .use_input(controller_1_use_input), .jump_addr(controller_1_jump_addr),
    .jump_enable(controller_1_jump_enable));
  ALU alu_1 (
    .A(output_a), .B(multiplexer_4_out), .opcode(controller_1_opcode), .F(alu_1_f), .Z(alu_1_z), .N(alu_1_n),
    .V(alu_1_v));
  regfile regfile_1 (
    .w_enable(controller_1_w_enable), .w_addr(controller_1_w_addr), .w_data(alu_1_f),
    .r_addr_a(controller_1_r_addr_a), .r_addr_b(controller_1_r_addr_b), .reset(reset), .clock(clock_1_out),
    .r_data_a(output_a), .r_data_b(output_b));

  // Notes on the sheet:
  //   contents of rom_1 (hex, n*v repeats v):
  //   144 148 14c a1 ce 17f 103
endmodule

module regfile (
  input  w_enable,
  input  [1:0] w_addr,
  input  [3:0] w_data,
  input  [1:0] r_addr_a,
  input  [1:0] r_addr_b,
  input  reset,
  input  clock,
  output [3:0] r_data_a,
  output [3:0] r_data_b
);

  wire decoder_1_out0, decoder_1_out1, decoder_1_out2, decoder_1_out3, decoder_2_out0, decoder_2_out1,
       decoder_2_out2, decoder_2_out3, decoder_3_out0, decoder_3_out1, decoder_3_out2, decoder_3_out3;
  wire [3:0] fourbitregister_1_q0, fourbitregister_2_q0, fourbitregister_3_q0, fourbitregister_4_q0;

  Decoder #(.select(2)) decoder_1 (
    .out0(decoder_1_out0), .out1(decoder_1_out1), .out2(decoder_1_out2), .out3(decoder_1_out3), .sel(w_addr),
    .en(w_enable));
  Decoder #(.enable("false"), .select(2)) decoder_2 (
    .out0(decoder_2_out0), .out1(decoder_2_out1), .out2(decoder_2_out2), .out3(decoder_2_out3), .sel(r_addr_a));
  Decoder #(.enable("false"), .select(2)) decoder_3 (
    .out0(decoder_3_out0), .out1(decoder_3_out1), .out2(decoder_3_out2), .out3(decoder_3_out3), .sel(r_addr_b));
  FourBitRegister fourbitregister_1 (
    .D(w_data), .clk(clock), .WE(decoder_1_out0), .R(reset), .q0(fourbitregister_1_q0[0]),
    .q1(fourbitregister_1_q0[1]), .q2(fourbitregister_1_q0[2]), .q3(fourbitregister_1_q0[3]));
  FourBitRegister fourbitregister_2 (
    .D(w_data), .clk(clock), .WE(decoder_1_out1), .R(reset), .q0(fourbitregister_2_q0[0]),
    .q1(fourbitregister_2_q0[1]), .q2(fourbitregister_2_q0[2]), .q3(fourbitregister_2_q0[3]));
  FourBitRegister fourbitregister_3 (
    .D(w_data), .clk(clock), .WE(decoder_1_out2), .R(reset), .q0(fourbitregister_3_q0[0]),
    .q1(fourbitregister_3_q0[1]), .q2(fourbitregister_3_q0[2]), .q3(fourbitregister_3_q0[3]));
  FourBitRegister fourbitregister_4 (
    .D(w_data), .clk(clock), .WE(decoder_1_out3), .R(reset), .q0(fourbitregister_4_q0[0]),
    .q1(fourbitregister_4_q0[1]), .q2(fourbitregister_4_q0[2]), .q3(fourbitregister_4_q0[3]));
  assign r_data_a = decoder_2_out0 ? fourbitregister_1_q0 : 4'bz;  // Controlled_Buffer controlled_buffer_1
  assign r_data_a = decoder_2_out1 ? fourbitregister_2_q0 : 4'bz;  // Controlled_Buffer controlled_buffer_2
  assign r_data_a = decoder_2_out2 ? fourbitregister_3_q0 : 4'bz;  // Controlled_Buffer controlled_buffer_3
  assign r_data_a = decoder_2_out3 ? fourbitregister_4_q0 : 4'bz;  // Controlled_Buffer controlled_buffer_4
  assign r_data_b = decoder_3_out0 ? fourbitregister_1_q0 : 4'bz;  // Controlled_Buffer controlled_buffer_5
  assign r_data_b = decoder_3_out1 ? fourbitregister_2_q0 : 4'bz;  // Controlled_Buffer controlled_buffer_6
  assign r_data_b = decoder_3_out2 ? fourbitregister_3_q0 : 4'bz;  // Controlled_Buffer controlled_buffer_7
  assign r_data_b = decoder_3_out3 ? fourbitregister_4_q0 : 4'bz;  // Controlled_Buffer controlled_buffer_8
endmodule

module ProgramCounter (
  input  [3:0] jump_addr,
  input  jump_enable,
  input  clock,
  input  reset,
  output [3:0] i_addr
);

  wire [3:0] fulladder4bit_1_sum, multiplexer_1_out;

  FullAdder4bit fulladder4bit_1 (.cin(1'b1), .A(i_addr), .sum(fulladder4bit_1_sum));  // open: B, cout
  Multiplexer #(.width(4)) multiplexer_1 (
    .in0(fulladder4bit_1_sum), .in1(jump_addr), .out(multiplexer_1_out), .sel(jump_enable));
  FourBitRegister fourbitregister_1 (
    .D(multiplexer_1_out), .clk(clock), .WE(1'b1), .R(reset), .q0(i_addr[0]), .q1(i_addr[1]), .q2(i_addr[2]),
    .q3(i_addr[3]));
endmodule

module controller (
  input  [8:0] instruction,
  input  V,
  input  Z,
  input  N,
  output [1:0] r_addr_a,
  output [1:0] r_addr_b,
  output [1:0] w_addr,
  output [2:0] opcode,
  output w_enable,
  output use_input,
  output [3:0] jump_addr,
  output jump_enable
);

  wire branchornon_1_jump_enabled, brnchornov_1_jump_enabled, brnchornoz_1_jump_enabled,
       jumpaddr_1_jump_enabled;

  convertobinary convertobinary_1 (
    .in_1(instruction), .r_addr_b(jump_addr[1:0]), .r_addr_a(jump_addr[3:2]), .aluOpcode(opcode),
    .brnchFlag(w_enable), .USE_INPUT(use_input));
  jumpaddr jumpaddr_1 (.alu(opcode), .brnch(w_enable), .jump_enabled(jumpaddr_1_jump_enabled));
  BrnchOrNOV brnchornov_1 (.alu(opcode), .V(V), .Brnch(w_enable), .jump_enabled(brnchornov_1_jump_enabled));
  BrnchOrNOZ brnchornoz_1 (.alu(opcode), .Z(Z), .Brnch(w_enable), .jump_enabled(brnchornoz_1_jump_enabled));
  BranchOrNoN branchornon_1 (.alu(opcode), .N(N), .Brnch(w_enable), .jump_enabled(branchornon_1_jump_enabled));
  or or_1 (jump_enable, jumpaddr_1_jump_enabled, brnchornov_1_jump_enabled, brnchornoz_1_jump_enabled, branchornon_1_jump_enabled);

  assign r_addr_a = jump_addr[3:2];
  assign r_addr_b = jump_addr[1:0];
  assign w_addr = jump_addr[3:2];
endmodule

module PCLogic (
  input  d3,
  input  d2,
  input  d1,
  input  d0,
  output q3,
  output q2,
  output q1,
  output q0
);

  wire and_1_out, and_2_out, and_3_out, and_4_out, and_5_out, and_6_out, and_7_out, and_8_out, and_9_out,
       not_1_out, not_2_out, not_3_out;

  not not_1 (not_1_out, d3);
  not not_2 (not_2_out, d2);
  not not_3 (not_3_out, d1);
  not not_4 (q0, d0);
  and and_1 (and_1_out, not_1_out, d2, d1, d0);
  and and_2 (and_2_out, d3, not_2_out);
  and and_3 (and_3_out, d3, not_3_out);
  and and_4 (and_4_out, d3, q0);
  and and_5 (and_5_out, not_2_out, d1, d0);
  and and_6 (and_6_out, d2, not_3_out);
  and and_7 (and_7_out, d2, q0);
  and and_8 (and_8_out, not_3_out, d0);
  and and_9 (and_9_out, d1, q0);
  or or_1 (q3, and_1_out, and_2_out, and_3_out, and_4_out);
  or or_2 (q2, and_5_out, and_6_out, and_7_out);
  or or_3 (q1, and_8_out, and_9_out);
endmodule

module FourBitRegister (
  input  [3:0] D,
  input  clk,
  input  WE,
  input  R,
  output q0,
  output q1,
  output q2,
  output q3
);

  wire and_1_out, and_2_out, and_3_out, and_4_out;

  and and_1 (and_1_out, WE, D[3]);
  D_Flip_Flop d_ff_1 (.D(and_1_out), .clk(clk), .Q(q3), .reset(R));  // open: Qn, preset
  and and_2 (and_2_out, WE, D[2]);
  D_Flip_Flop d_ff_2 (.D(and_2_out), .clk(clk), .Q(q2), .reset(R));  // open: Qn, preset
  and and_3 (and_3_out, WE, D[1]);
  D_Flip_Flop d_ff_3 (.D(and_3_out), .clk(clk), .Q(q1), .reset(R));  // open: Qn, preset
  and and_4 (and_4_out, WE, D[0]);
  D_Flip_Flop d_ff_4 (.D(and_4_out), .clk(clk), .Q(q0), .reset(R));  // open: Qn, preset
endmodule

module enablerhelper (
  input  [3:0] Data,
  input  e,
  input  clk,
  output d0,
  output d1,
  output d2,
  output d3,
  output clkO
);

  and and_1 (d0, Data[0], e);
  and and_2 (d1, Data[1], e);
  and and_3 (d2, Data[2], e);
  and and_4 (d3, Data[3], e);
  and and_5 (clkO, e, clk);
endmodule

module convertobinary (
  input  [8:0] in_1,
  output [1:0] r_addr_b,
  output [1:0] r_addr_a,
  output [2:0] aluOpcode,
  output brnchFlag,
  output USE_INPUT
);


  assign aluOpcode = in_1[6:4];
  assign brnchFlag = in_1[7];
  assign r_addr_a = in_1[3:2];
  assign r_addr_b = in_1[1:0];
  assign USE_INPUT = in_1[8];
endmodule

module BrnchOrNOV (
  input  [2:0] alu,
  input  V,
  input  Brnch,
  output jump_enabled
);

  wire and_1_out, and_2_out, not_1_out, not_2_out, not_3_out, not_4_out;

  not not_1 (not_1_out, alu[0]);
  not not_2 (not_2_out, alu[2]);
  not not_3 (not_3_out, V);
  not not_4 (not_4_out, alu[2]);
  and and_1 (and_1_out, not_1_out, alu[1], not_2_out, not_3_out, Brnch);
  and and_2 (and_2_out, alu[0], alu[1], not_4_out, V, Brnch);
  or or_1 (jump_enabled, and_1_out, and_2_out);
endmodule

module BrnchOrNOZ (
  input  [2:0] alu,
  input  Z,
  input  Brnch,
  output jump_enabled
);

  wire and_1_out, and_2_out, not_1_out, not_2_out, not_3_out, not_4_out;

  not not_1 (not_1_out, alu[1]);
  not not_2 (not_2_out, alu[0]);
  and and_1 (and_1_out, alu[2], not_1_out, not_2_out, not_3_out, Brnch);
  not not_3 (not_3_out, Z);
  not not_4 (not_4_out, alu[1]);
  and and_2 (and_2_out, alu[2], not_4_out, alu[0], Z, Brnch);
  or or_1 (jump_enabled, and_1_out, and_2_out);
endmodule

module BranchOrNoN (
  input  [2:0] alu,
  input  N,
  input  Brnch,
  output jump_enabled
);

  wire and_1_out, and_2_out, not_1_out, not_2_out;

  not not_1 (not_1_out, alu[0]);
  not not_2 (not_2_out, N);
  and and_1 (and_1_out, alu[1], alu[2], not_1_out, not_2_out, Brnch);
  and and_2 (and_2_out, alu[1], alu[2], alu[0], N, Brnch);
  or or_1 (jump_enabled, and_1_out, and_2_out);
endmodule

module jumpaddr (
  input  [2:0] alu,
  input  brnch,
  output jump_enabled
);

  wire not_1_out, not_2_out, not_3_out;

  not not_1 (not_1_out, alu[2]);
  not not_2 (not_2_out, alu[1]);
  and and_1 (jump_enabled, not_1_out, not_2_out, not_3_out, brnch);
  not not_3 (not_3_out, alu[0]);
endmodule
